// Logisim project alu.circ as structural Verilog: 11 circuits, main circuit main
module main (
);

  wire arithmatic_unit_1_y_0, arithmatic_unit_1_y_1, arithmatic_unit_1_y_2, arithmatic_unit_1_y_3,
       logic_unit_1_y0, logic_unit_1_y1, logic_unit_1_y2, logic_unit_1_y3, undriven;

  Arithmatic_unit arithmatic_unit_1 (
    .Y_3(arithmatic_unit_1_y_3), .Y_2(arithmatic_unit_1_y_2), .Y_1(arithmatic_unit_1_y_1),
    .Y_0(arithmatic_unit_1_y_0));  // open: A_3, A_2, A_1, A_0, B_3, B_2, B_1, B_0, D_4, D_3, D_2, D_1, Carry, OV
  Logic_unit logic_unit_1 (
    .Y3(logic_unit_1_y3), .Y2(logic_unit_1_y2), .Y1(logic_unit_1_y1), .Y0(logic_unit_1_y0));  // open: A0, A1, A2, A3, B0, B1, B2, B3
  Mux_4bit mux_4bit_1 (
    .A_3(arithmatic_unit_1_y_3), .A_2(arithmatic_unit_1_y_2), .A_1(arithmatic_unit_1_y_1),
    .A_0(arithmatic_unit_1_y_0), .B_3(logic_unit_1_y3), .B_2(logic_unit_1_y2), .B_1(logic_unit_1_y1),
    .B_0(logic_unit_1_y0), .S(undriven));  // open: Y_3, Y_2, Y_1, Y_0
endmodule

module One_bit_and (
  input  I_3,
  input  I_2,
  input  I_1,
  input  I_0,
  input  C,
  output Y_3,
  output Y_2,
  output Y_1,
  output Y_0
);

  // DIP_7408 dip_7408_1: pin names not known; wires that end beside it: I_2, C, Y_2, C, I_1, Y_1, I_3, C, Y_3, C, I_0, Y_0
endmodule

module one_bit_xor (
  input  I_3,
  input  I_2,
  input  I_1,
  input  I_0,
  input  C,
  output Y_3,
  output Y_2,
  output Y_1,
  output Y_0
);

  // DIP_7486 dip_7486_1: pin names not known; wires that end beside it: I_3, C, Y_3, I_2, C, Y_2, I_1, C, Y_1, C, I_0, Y_0
endmodule

module test (
  input  in_1,
  input  in_2,
  output out_3
);

  // DIP_7408 dip_7408_1: pin names not known; wires that end beside it: in_1, in_2, out_3
endmodule

module adder_helper (
  input  A_3,
  input  A_2,
  input  A_1,
  input  A_0,
  input  B_3,
  input  B_2,
  input  B_1,
  input  B_0,
  input  C_in,
  output Y_3,
  output Y_2,
  output Y_1,
  output Y_0,
  output C_out
);

  // DIP_74283 dip_74283_1: pin names not known; wires that end beside it: Y_1, B_1, A_1, Y_0, A_0, B_0, C_in, B_2, A_2, Y_2, A_3, B_3, Y_3, C_out
endmodule

module my_74283 (
  input  CIN,
  input  A1,
  input  B1,
  input  A2,
  input  B2,
  input  A3,
  input  B3,
  input  A4,
  input  B4,
  output Y1,
  output Y2,
  output Y3,
  output Y4,
  output COUT
);

  wire and_1_out, and_2_out, and_3_out, and_4_out, and_5_out, and_6_out, and_7_out, and_8_out, and_9_out,
       and_10_out, and_11_out, and_12_out, and_13_out, and_14_out, nand_1_out, nand_2_out, nand_3_out,
       nand_4_out, nor_1_out, nor_2_out, nor_3_out, nor_4_out, nor_5_out, nor_6_out, nor_7_out, not_1_out,
       not_2_out, not_3_out, not_4_out, not_5_out, not_6_out;

  not not_1 (not_1_out, CIN);
  nor nor_1 (nor_1_out, A1, B1);
  nand nand_1 (nand_1_out, A1, B1);
  nor nor_2 (nor_2_out, A2, B2);
  nand nand_2 (nand_2_out, A2, B2);
  nor nor_3 (nor_3_out, A3, B3);
  nand nand_3 (nand_3_out, A3, B3);
  nor nor_4 (nor_4_out, A4, B4);
  nand nand_4 (nand_4_out, A4, B4);
  not not_2 (not_2_out, not_1_out);
  not not_3 (not_3_out, nor_1_out);
  and and_1 (and_1_out, not_1_out, nand_1_out);
  not not_4 (not_4_out, nor_2_out);
  and and_2 (and_2_out, not_1_out, nand_1_out, nand_2_out);
  and and_3 (and_3_out, nand_2_out, nor_1_out);
  not not_5 (not_5_out, nor_3_out);
  and and_4 (and_4_out, not_1_out, nand_1_out, nand_2_out, nand_3_out);
  and and_5 (and_5_out, nand_2_out, nand_3_out, nor_1_out);
  and and_6 (and_6_out, nand_3_out, nor_2_out);
  not not_6 (not_6_out, nor_4_out);
  and and_7 (and_7_out, not_1_out, nand_1_out, nand_2_out, nand_3_out, nand_4_out);
  and and_8 (and_8_out, nand_2_out, nand_3_out, nand_4_out, nor_1_out);
  and and_9 (and_9_out, nand_3_out, nand_4_out, nor_2_out);
  and and_10 (and_10_out, nand_4_out, nor_3_out);
  and and_11 (and_11_out, not_3_out, nand_1_out);
  nor nor_5 (nor_5_out, and_1_out, nor_1_out);
  and and_12 (and_12_out, not_4_out, nand_2_out);
  nor nor_6 (nor_6_out, and_2_out, and_3_out, nor_2_out);
  and and_13 (and_13_out, not_5_out, nand_3_out);
  nor nor_7 (nor_7_out, and_4_out, and_5_out, and_6_out, nor_3_out);
  and and_14 (and_14_out, not_6_out, nand_4_out);
  nor nor_8 (COUT, and_7_out, and_8_out, and_9_out, and_10_out, nor_4_out);
  xor xor_1 (Y1, not_2_out, and_11_out);
  xor xor_2 (Y2, nor_5_out, and_12_out);
  xor xor_3 (Y3, nor_6_out, and_13_out);
  xor xor_4 (Y4, nor_7_out, and_14_out);
endmodule

module adder_helper_2 (
  input  A_3,
  input  A_2,
  input  A_1,
  input  A_0,
  input  B_3,
  input  B_2,
  input  B_1,
  input  B_0,
  input  C_in,
  output Y_3,
  output Y_2,
  output Y_1,
  output Y_0,
  output C_out,
  output OV
);

  my_74283 my_74283_1 (
    .CIN(C_in), .A1(A_0), .B1(B_0), .A2(A_1), .B2(B_1), .A3(A_2), .B3(B_2), .A4(A_3), .B4(B_3), .Y1(Y_0),
    .Y2(Y_1), .Y3(Y_2), .Y4(Y_3), .COUT(C_out));
  overflow_bit_detector overflow_bit_detector_1 (.A3(A_3), .B3(B_3), .S3(Y_3), .Overflow_bit(OV));
endmodule

module overflow_bit_detector (
  input  A3,
  input  B3,
  input  S3,
  output Overflow_bit
);

  wire dip_7404_1_p2, dip_7404_1_p4, dip_7408_1_p3, dip_7432_1_p3, dip_7432_1_p4, dip_7432_1_p5;

  // DIP_7432 dip_7432_1: pin names not known; wires that end beside it: B3, A3, dip_7432_1_p3, dip_7432_1_p4, dip_7432_1_p5, Overflow_bit
  // DIP_7404 dip_7404_1: pin names not known; wires that end beside it: dip_7432_1_p3, dip_7404_1_p2, S3, dip_7404_1_p4
  // DIP_7408 dip_7408_1: pin names not known; wires that end beside it: A3, B3, dip_7408_1_p3, S3, dip_7404_1_p2, dip_7432_1_p5, dip_7408_1_p3, dip_7404_1_p4, dip_7432_1_p4
endmodule

module Arithmatic_unit (
  input  A_3,
  input  A_2,
  input  A_1,
  input  A_0,
  input  B_3,
  input  B_2,
  input  B_1,
  input  B_0,
  input  D_4,
  input  D_3,
  input  D_2,
  input  D_1,
  output Y_3,
  output Y_2,
  output Y_1,
  output Y_0,
  output Carry,
  output OV
);

  wire one_bit_and_1_y_0, one_bit_and_1_y_1, one_bit_and_1_y_2, one_bit_and_1_y_3, one_bit_xor_1_y_0,
       one_bit_xor_1_y_1, one_bit_xor_1_y_2, one_bit_xor_1_y_3, one_bit_xor_2_y_0, one_bit_xor_2_y_1,
       one_bit_xor_2_y_2, one_bit_xor_2_y_3;

  one_bit_xor one_bit_xor_1 (
    .I_3(A_3), .I_2(A_2), .I_1(A_1), .I_0(A_0), .C(D_1), .Y_3(one_bit_xor_1_y_3), .Y_2(one_bit_xor_1_y_2),
    .Y_1(one_bit_xor_1_y_1), .Y_0(one_bit_xor_1_y_0));
  One_bit_and one_bit_and_1 (
    .I_3(B_3), .I_2(B_2), .I_1(B_1), .I_0(B_0), .C(D_2), .Y_3(one_bit_and_1_y_3), .Y_2(one_bit_and_1_y_2),
    .Y_1(one_bit_and_1_y_1), .Y_0(one_bit_and_1_y_0));
  one_bit_xor one_bit_xor_2 (
    .I_3(one_bit_and_1_y_3), .I_2(one_bit_and_1_y_2), .I_1(one_bit_and_1_y_1), .I_0(one_bit_and_1_y_0),
    .C(D_3), .Y_3(one_bit_xor_2_y_3), .Y_2(one_bit_xor_2_y_2), .Y_1(one_bit_xor_2_y_1),
    .Y_0(one_bit_xor_2_y_0));
  adder_helper_2 adder_helper_2_1 (
    .A_3(one_bit_xor_1_y_3), .A_2(one_bit_xor_1_y_2), .A_1(one_bit_xor_1_y_1), .A_0(one_bit_xor_1_y_0),
    .B_3(one_bit_xor_2_y_3), .B_2(one_bit_xor_2_y_2), .B_1(one_bit_xor_2_y_1), .B_0(one_bit_xor_2_y_0),
    .C_in(D_4), .Y_3(Y_3), .Y_2(Y_2), .Y_1(Y_1), .Y_0(Y_0), .C_out(Carry), .OV(OV));
endmodule

module Logic_unit (
  input  A0,
  input  A1,
  input  A2,
  input  A3,
  input  B0,
  input  B1,
  input  B2,
  input  B3,
  output Y3,
  output Y2,
  output Y1,
  output Y0
);

  // DIP_7432 dip_7432_1: pin names not known; wires that end beside it: A0, B0, Y0, B1, A1, Y1, A2, B2, Y2, A3, B3, Y3
endmodule

module Mux_4bit (
  input  A_3,
  input  A_2,
  input  A_1,
  input  A_0,
  input  B_3,
  input  B_2,
  input  B_1,
  input  B_0,
  input  S,
  output Y_3,
  output Y_2,
  output Y_1,
  output Y_0
);

  // DIP_74157 dip_74157_1: pin names not known; wires that end beside it: S, A_3, B_3, Y_3, A_2, B_2, Y_2, A_1, B_1, Y_1, A_0, B_0, Y_0
endmodule
